# Fritzing sketch fritzing (saved by Fritzing 0.9.3b)
breadboards: 1

parts:
  Raspberry_Pi_1 = Raspberry Pi 3 [part_number=RPI-3-V1.2]
  R1 = Resistor [tolerance=±5% resistance=330 package="1206 [SMD]"]
  R2 = Resistor [tolerance=±5% resistance=330 package="1206 [SMD]"]
  LED1 = smd LED [color="Red (633nm)" package="1206 [SMD]"]
  LED2 = smd LED [color="Green (565nm)" package="1206 [SMD]"]
  S1 = Pushbutton [package="[THT]"]
  S2 = Pushbutton [package="[THT]"]
  R3 = Resistor [tolerance=±5% resistance=330 package="1206 [SMD]"]
  R4 = Resistor [tolerance=±5% resistance=330 package="1206 [SMD]"]

nets:
  3V3: Raspberry_Pi_1.3v3, Raspberry_Pi_1.3V3, Raspberry_Pi_1.GPIO9, R1.Pin_0, R2.Pin_0, S1.Pin_3, S1.Pin_4, S2.Pin_1, S2.Pin_2, S2.Pin_3, S2.Pin_4, R4.Pin_1
  N1: Raspberry_Pi_1.GND, R3.Pin_0, R4.Pin_0
  N2: Raspberry_Pi_1.GPIO17, Raspberry_Pi_1.GPIO6, LED1.anode
  N3: Raspberry_Pi_1.GPIO27, LED2.anode
  N4: Raspberry_Pi_1.GPIO22, S1.Pin_1, S1.Pin_2, R3.Pin_1
  N5: R1.Pin_1, LED2.cathode
  N6: R2.Pin_1, LED1.cathode
